# Fritzing sketch Encoder Fixture (saved by Fritzing 0.9.9b)
breadboards: 1

parts:
  Q1 = MOSFET-NCHANNEL [package=to220v]
  M1 = Raspberry Pi Pico
  R1 = Resistor [tolerance=±5% resistance=160 package="0805 [SMD]"]
  R2 = Resistor [tolerance=±5% resistance=5.1k package="0805 [SMD]"]
  R3 = Resistor [tolerance=±5% resistance=5.1k package="0805 [SMD]"]
  J1 = female pin header, 6 pins [form="♀ (female)"]
  LED1 = RGB LED (com. cathode, rgb) [package="5 mm [THT]"]
  J2 = female pin header, 4 pins [form="♀ (female)"]
  R4 = Resistor [tolerance=±5% power=0.25 resistance=220 package=THT]
  R5 = Resistor [tolerance=±5% power=0.25 resistance=220 package=THT]
  R6 = Resistor [tolerance=±5% power=0.25 resistance=220 package=THT]

nets:
  N1: Q1.G, M1.pin_19
  N2: Q1.D, J1.pin5
  GND: Q1.S, M1.pin_3, M1.pin_8, M1.pin_13, M1.pin_18, M1.pin_23, M1.pin_28, M1.pin_33, M1.pin_38, R1.Pin_0, R2.Pin_0, R3.Pin_0, LED1.common_cathode, J2.pin1
  N3: M1.pin_4, J2.pin4
  N4: M1.pin_5, J2.pin3
  N5: M1.pin_15, R6.Pin_1
  N6: M1.pin_16, R5.Pin_1
  N7: M1.pin_17, R4.Pin_1
  N8: M1.pin_20, M1.pin_34, R1.Pin_1, J1.pin1
  N9: M1.pin_31, R3.Pin_1, J1.pin2
  N10: M1.pin_32, R2.Pin_1, J1.pin3
  N11: M1.pin_36, J1.pin4, J1.pin6, J2.pin2
  N12: LED1.red_anode, R6.Pin_0
  N13: LED1.green_anode, R5.Pin_0
  N14: LED1.blue_anode, R4.Pin_0

custom parts:
  Raspberry Pi Pico: Raspberry Pi Pico. Based around the RP2040 microcontroller the Pico is a low cost microcontroller device bringing Raspberry Pi quality, cost, and easy of use to the microcontroller space. Jan 2021, Split part in to two versions: SMD (this one) and tht. This one is single sided and uses the castellation pads to solder the module to the board (no holes, other than for the USB connector!). The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
